# Fritzing sketch new (saved by Fritzing 0.9.3b)
perfboards: 1

parts:
  Componente1 = Arduino Micro (Rev3)
  LED1 = LED - 5mm [color="Green (555nm)" package="5 mm [THT]"]
  LED2 = LED - 5mm [color="Red (633nm)" package="5 mm [THT]"]
  LED4 = LED - 5mm [color="Blue (430nm)" package="5 mm [THT]"]
  LED5 = LED - 3mm [color="Red (633nm)" package="3 mm [THT]"]
  LED3 = LED - 3mm [color="Red (633nm)" package="3 mm [THT]"]
  LED6 = LED - 3mm [color="Red (633nm)" package="3 mm [THT]"]
  S1 = Round Pushbutton
  S2 = Round Pushbutton  # not connected
  S3 = Round Pushbutton
  S4 = Round Pushbutton
  S5 = Round Pushbutton  # not connected
  R1 = Resistor [tolerance=±5% resistance=220 package=THT]
  R2 = Resistor [tolerance=±5% resistance=220 package=THT]
  R3 = Resistor [tolerance=±5% resistance=220 package=THT]
  R4 = Resistor [tolerance=±5% resistance=220 package=THT]
  R5 = Resistor [tolerance=±5% resistance=220 package=THT]
  R6 = Resistor [tolerance=±5% resistance=220 package=THT]

nets:
  N1: Componente1.D2/SDA, S1.leg0
  N2: Componente1.D3/SCL, R1.Pin_0
  N3: Componente1.D5_PWM, R2.Pin_0
  N4: Componente1.D6_PWM/A7, S3.leg0
  N5: Componente1.D7, R3.Pin_0
  N6: Componente1.D8_PWM/A8, S4.leg0
  N7: Componente1.D9_PWM/A9, R4.Pin_0
  N8: Componente1.D11_PWM, R6.Pin_0
  N9: Componente1.D12_PWM/A11, R5.Pin_0
  N10: Componente1.GND, LED6.anode
  N11: LED1.cathode, R4.Pin_1
  N12: LED2.cathode, R6.Pin_1
  N13: LED4.cathode, R5.Pin_1
  N14: LED5.cathode, R2.Pin_1
  N15: LED3.cathode, R3.Pin_1
  N16: LED6.cathode, R1.Pin_1
